// Logisim project ax8.circ as structural Verilog
module full_adder_x1 (
  input  A,
  input  B,
  input  Cin,
  output Y,
  output Cout
);

  wire and_1_out, and_2_out, xor_1_out;

  xor xor_1 (xor_1_out, A, B);
  and and_1 (and_1_out, xor_1_out, Cin);
  and and_2 (and_2_out, A, B);
  xor xor_2 (Y, xor_1_out, Cin);
  or or_1 (Cout, and_1_out, and_2_out);
endmodule

module full_adder_x4 (
  input  [3:0] A,
  input  [3:0] B,
  input  Cin,
  output [3:0] Y,
  output Cout
);

  wire full_adder_x1_1_cout, full_adder_x1_2_cout, full_adder_x1_3_cout;

  full_adder_x1 full_adder_x1_1 (.A(A[0]), .B(B[0]), .Cin(Cin), .Y(Y[0]), .Cout(full_adder_x1_1_cout));
  full_adder_x1 full_adder_x1_2 (.A(A[1]), .B(B[1]), .Cin(full_adder_x1_1_cout), .Y(Y[1]), .Cout(full_adder_x1_2_cout));
  full_adder_x1 full_adder_x1_3 (.A(A[2]), .B(B[2]), .Cin(full_adder_x1_2_cout), .Y(Y[2]), .Cout(full_adder_x1_3_cout));
  full_adder_x1 full_adder_x1_4 (.A(A[3]), .B(B[3]), .Cin(full_adder_x1_3_cout), .Y(Y[3]), .Cout(Cout));
endmodule

module sr_flip_flop (
  input  R,
  input  CLK,
  input  S,
  output Q,
  output NQ
);

  wire and_1_out, and_2_out;

  and and_1 (and_1_out, R, CLK);
  and and_2 (and_2_out, CLK, S);
  nor nor_1 (Q, and_1_out, NQ);
  nor nor_2 (NQ, Q, and_2_out);
endmodule
